# Fritzing sketch dual ring clock schematic (saved by Fritzing 0.8.7b)
breadboards: 1

parts:
  Part1 = Arduino Micro (Rev3)
  S1 = Momentary Switch [package=ksa_sealed_tac_switch]
  S2 = Momentary Switch [package=ksa_sealed_tac_switch]
  S3 = Momentary Switch [package=ksa_sealed_tac_switch]
  S4 = Momentary Switch [package=ksa_sealed_tac_switch]
  C1 = Electrolytic Capacitor [capacitance=1000μF voltage=35V package="1010 [SMD, electrolytic]"]
  neopixel1 = Neopixel Ring 12
  neopixel2 = Neopixel 24 Ring
  RTC1 = DS1307 RTC Breakout
  R1 = Resistor [tolerance=±5% resistance=470 package="1206 [SMD]"]
  R3 = Resistor [tolerance=±5% resistance=470 package="1206 [SMD]"]

nets:
  N1: Part1.D2/SDA, RTC1.SDA
  N2: Part1.D3/SCL, RTC1.SCL
  N3: Part1.D5_PWM, R3.Pin_0
  N4: Part1.D6_PWM/A7, R1.Pin_0
  N5: Part1.D7, S4.3
  N6: Part1.D8_PWM/A8, S3.3
  N7: Part1.D9_PWM/A9, S2.3
  N8: Part1.D10_PWM/A10, S1.3
  GND: Part1.VIN, S1.2, S2.2, S3.2, S4.2, C1.-, neopixel1.GND, neopixel2.GND, RTC1.GND
  5V: Part1.5V, C1.+, neopixel1.VCC, neopixel2.Vcc, RTC1.5V
  N9: neopixel1.IN, R3.Pin_1
  N10: neopixel2.IN, R1.Pin_1

notes:
  I used a ChronoDot instead of the DS1307 RTC

custom parts:
  Neopixel Ring 12: Neopixel Ring x12
  DS1307 RTC Breakout: DS1307 Real-time Clock Breakout Board with Battery
